// Logisim project DIGITAL1.circ as structural Verilog: 1 circuit, main circuit main
module main (
  input  A,
  input  B,
  input  C,
  input  D,
  input  B_2,
  input  D_2
);

  wire and_1_out, and_2_out, and_3_out, and_4_out, and_5_out, and_6_out, and_7_out, and_8_out, and_9_out,
       and_10_out, not_1_out, not_2_out, not_3_out, not_4_out, not_5_out, not_6_out, or_1_out, or_2_out;

  not not_1 (not_1_out, A);
  not not_2 (not_2_out, B);
  not not_3 (not_3_out, B_2);
  not not_4 (not_4_out, C);
  not not_5 (not_5_out, D_2);
  not not_6 (not_6_out, D);
  and and_1 (and_1_out, not_1_out, not_6_out, C, not_2_out);
  and and_2 (and_2_out, not_1_out, not_2_out, not_4_out, not_6_out);
  and and_3 (and_3_out, not_5_out, not_3_out);
  and and_4 (and_4_out, B_2, D_2);
  and and_5 (and_5_out, not_1_out, B, not_4_out, D);
  and and_6 (and_6_out, not_1_out, B, C, D);
  and and_7 (and_7_out, A, not_2_out, not_4_out, not_6_out);
  and and_8 (and_8_out, A, not_2_out, C, not_6_out);
  and and_9 (and_9_out, A, B, D, not_4_out);
  and and_10 (and_10_out, A, B, C, D);
  or or_1 (or_1_out, and_3_out, and_4_out);
  LED led_1 (.in(or_1_out));
  or or_2 (or_2_out, and_1_out, and_2_out, and_5_out, and_6_out, and_7_out, and_8_out, and_9_out, and_10_out);
  LED led_2 (.in(or_2_out));
endmodule
