// Logisim project DIGITAL3.circ as structural Verilog: 1 circuit, main circuit main
module main (
  input  PIN
);

  wire and_1_out, and_2_out, and_3_out, and_4_out, and_5_out, and_6_out, clock_1_out, d_ff_1_q, d_ff_1_qn,
       d_ff_2_q, d_ff_2_qn, or_1_out;

  Clock clock_1 (.out(clock_1_out));
  and and_1 (and_1_out, d_ff_1_qn, d_ff_2_qn, PIN);
  and and_2 (and_2_out, d_ff_2_qn, d_ff_1_q);
  and and_3 (and_3_out, d_ff_2_q, d_ff_1_qn, PIN);
  D_Flip_Flop d_ff_1 (.D(and_3_out), .clk(clock_1_out), .Q(d_ff_1_q), .Qn(d_ff_1_qn));  // open: preset, reset
  D_Flip_Flop d_ff_2 (.D(or_1_out), .clk(clock_1_out), .Q(d_ff_2_q), .Qn(d_ff_2_qn));  // open: preset, reset
  or or_1 (or_1_out, and_1_out, and_2_out);
  and and_4 (and_4_out, d_ff_1_qn, d_ff_2_qn);
  LED led_1 (.in(and_4_out));
  LED led_2 (.in(and_5_out));
  and and_5 (and_5_out, d_ff_1_qn, d_ff_2_q);
  and and_6 (and_6_out, d_ff_2_qn, d_ff_1_q);
  LED led_3 (.in(and_6_out));
  LED led_4 (.in(and_6_out));
  LED led_5 (.in(d_ff_1_qn));

  // Notes on the sheet:
  //   P INPUT 
  //   VG
  //   VY
  //   VR
  //   PW
  //   PR
endmodule
