// Logisim project LLL.circ as structural Verilog: 1 circuit, main circuit main
module main (
  input  in_1
);

  wire and_1_out, clock_1_out, clock_2_out, d_ff_1_q, d_ff_1_qn, j_k_ff_1_q, j_k_ff_2_q, j_k_ff_3_q,
       j_k_ff_4_q;

  D_Flip_Flop d_ff_1 (.D(in_1), .clk(clock_1_out), .Q(d_ff_1_q), .Qn(d_ff_1_qn));  // open: preset, reset
  Clock clock_1 (.out(clock_1_out));
  Clock clock_2 (.out(clock_2_out));
  J_K_Flip_Flop j_k_ff_1 (
    .J(1'b1), .K(1'b1), .clk(clock_2_out), .Q(j_k_ff_1_q), .reset(and_1_out));  // open: Qn, preset
  LED led_1 (.in(d_ff_1_q));
  LED led_2 (.in(d_ff_1_qn));
  LED led_3 (.in(j_k_ff_1_q));
  J_K_Flip_Flop j_k_ff_2 (.J(1'b1), .K(1'b1), .clk(j_k_ff_1_q), .Q(j_k_ff_2_q), .reset(and_1_out));  // open: Qn, preset
  LED led_4 (.in(j_k_ff_2_q));
  J_K_Flip_Flop j_k_ff_3 (.J(1'b1), .K(1'b1), .clk(j_k_ff_2_q), .Q(j_k_ff_3_q), .reset(and_1_out));  // open: Qn, preset
  and and_1 (and_1_out, 1'b1, j_k_ff_4_q);
  LED led_5 (.in(j_k_ff_3_q));
  J_K_Flip_Flop j_k_ff_4 (.J(1'b1), .K(1'b1), .clk(j_k_ff_3_q), .Q(j_k_ff_4_q), .reset(and_1_out));  // open: Qn, preset
  LED led_6 (.in(j_k_ff_4_q));

  // Notes on the sheet:
  //   D
  //   C
  //   B
  //   A
endmodule
