// Logisim project kkk.circ as structural Verilog: 1 circuit, main circuit main
module main (
  input  [3:0] INPUT_B,
  input  [3:0] Input_A,
  input  [1:0] in_3,
  output [3:0] OUTPUT
);

  wire [3:0] adder_1_out, and_1_out, or_1_out, subtractor_1_out;

  Adder #(.width(4)) adder_1 (.a(Input_A), .b(INPUT_B), .out(adder_1_out));  // open: cin, cout
  Multiplexer #(.select(2), .width(4)) multiplexer_1 (
    .in0(adder_1_out), .in1(subtractor_1_out), .in2(and_1_out), .in3(or_1_out), .out(OUTPUT), .sel(in_3));
  Subtractor #(.width(4)) subtractor_1 (.a(Input_A), .b(INPUT_B), .out(subtractor_1_out));  // open: bin, bout
  assign and_1_out = Input_A & INPUT_B;  // AND_Gate and_1, 4 bits wide
  assign or_1_out = Input_A | INPUT_B;  // OR_Gate or_1, 4 bits wide

  // Notes on the sheet:
  //   SELECT
  //   ADD
  //   SUBSTRACT
  //   AND
  //   OR
endmodule
