// Logisim project ppp.circ as structural Verilog: 1 circuit, main circuit main
module main (
  output out_1,
  output out_2,
  output out_3
);

  wire and_1_out, clock_1_out, j_k_ff_3_q;

  J_K_Flip_Flop j_k_ff_1 (.J(1'b1), .K(1'b1), .clk(clock_1_out), .Q(out_1));  // open: Qn, preset, reset
  Clock clock_1 (.out(clock_1_out));
  J_K_Flip_Flop j_k_ff_2 (.J(out_1), .K(out_1), .clk(clock_1_out), .Q(out_3));  // open: Qn, preset, reset
  J_K_Flip_Flop j_k_ff_3 (.J(out_3), .K(out_3), .clk(clock_1_out), .Q(j_k_ff_3_q));  // open: Qn, preset, reset
  and and_1 (and_1_out, out_1, out_3, j_k_ff_3_q);
  J_K_Flip_Flop j_k_ff_4 (.J(and_1_out), .K(and_1_out), .clk(clock_1_out), .Q(out_2));  // open: Qn, preset, reset
endmodule
