// Logisim project project7.circ as structural Verilog: 1 circuit, main circuit main
module main (
  input  ENTRANCE,
  input  CLEARANCE
);

  wire and_1_out, and_2_out, and_3_out, and_4_out, clock_1_out, d_ff_1_q, d_ff_1_qn, ff1_qn, not_1_out,
       or_1_out;

  Clock clock_1 (.out(clock_1_out));
  and and_1 (and_1_out, d_ff_1_q, CLEARANCE, ff1_qn);
  D_Flip_Flop ff1 (.D(and_1_out), .clk(clock_1_out), .Qn(ff1_qn));  // open: Q, preset, reset
  not not_1 (not_1_out, CLEARANCE);
  D_Flip_Flop d_ff_1 (.D(and_2_out), .clk(clock_1_out), .Q(d_ff_1_q), .Qn(d_ff_1_qn));  // open: preset, reset
  and and_2 (and_2_out, ff1_qn, or_1_out);
  and and_3 (and_3_out, ENTRANCE, d_ff_1_qn);
  and and_4 (and_4_out, not_1_out, d_ff_1_q);
  or or_1 (or_1_out, and_3_out, and_4_out);
  LED led_1 (.in(d_ff_1_q));
  LED led_2 (.in(d_ff_1_qn));

  // Notes on the sheet:
  //   G
  //   L
endmodule
