// Logisim project zzz.circ as structural Verilog: 1 circuit, main circuit main
module main (
  input  [1:0] A,
  input  [1:0] B,
  output [1:0] o_p
);

  wire comparator_1_gt;

  Comparator #(.width(2)) comparator_1 (.a(A), .b(B), .gt(comparator_1_gt));  // open: eq, lt
  Multiplexer #(.width(2)) multiplexer_1 (.in0(A), .in1(B), .out(o_p), .sel(comparator_1_gt));
endmodule
